// Logisim project 5.circ as structural Verilog
module \Задание_1  (
  input  [7:0] in_1,
  input  \Включение ,
  input  \Вход_синхронизации ,
  input  \Сброс_значения ,
  output [7:0] out_5
);

  Register register_1 (.D(in_1), .en(\Включение ), .Q(out_5), .clk(\Вход_синхронизации ), .clr(\Сброс_значения ));
endmodule

module \Задание_2  (
  input  in_1,
  input  in_2,
  input  in_3,
  input  in_4,
  input  in_5,
  input  in_6,
  input  in_7,
  input  in_8,
  input  in_9,
  output out_10,
  output out_11,
  output out_12,
  output out_13,
  output out_14,
  output out_15,
  output out_16,
  output out_17
);

  D_Flip_Flop d_ff_1 (.clk(in_4), .D(in_1), .Q(out_10));  // open: Qn, preset, en, reset
  D_Flip_Flop d_ff_2 (.clk(in_4), .D(in_2), .Q(out_11));  // open: Qn, preset, en, reset
  D_Flip_Flop d_ff_3 (.clk(in_4), .D(in_3), .Q(out_12));  // open: Qn, preset, en, reset
  D_Flip_Flop d_ff_4 (.clk(in_4), .D(in_5), .Q(out_13));  // open: Qn, preset, en, reset
  D_Flip_Flop d_ff_5 (.clk(in_4), .D(in_6), .Q(out_14));  // open: Qn, preset, en, reset
  D_Flip_Flop d_ff_6 (.clk(in_4), .D(in_7), .Q(out_15));  // open: Qn, preset, en, reset
  D_Flip_Flop d_ff_7 (.clk(in_4), .D(in_8), .Q(out_16));  // open: Qn, preset, en, reset
  D_Flip_Flop d_ff_8 (.clk(in_4), .D(in_9), .Q(out_17));  // open: Qn, preset, en, reset
endmodule

module \Задание_3  (
  input  \Такт ,
  input  \Бит ,
  input  \Очистка 
);

  wire d_ff_1_q, d_ff_2_q, d_ff_3_q;

  D_Flip_Flop d_ff_1 (.clk(\Такт ), .D(\Бит ), .Q(d_ff_1_q), .reset(\Очистка ));  // open: Qn, preset, en
  D_Flip_Flop d_ff_2 (.clk(\Такт ), .D(d_ff_1_q), .Q(d_ff_2_q), .reset(\Очистка ));  // open: Qn, preset, en
  D_Flip_Flop d_ff_3 (.clk(\Такт ), .D(d_ff_2_q), .Q(d_ff_3_q), .reset(\Очистка ));  // open: Qn, preset, en
  D_Flip_Flop d_ff_4 (.clk(\Такт ), .D(d_ff_3_q), .reset(\Очистка ));  // open: Q, Qn, preset, en
endmodule

module \Задание_4  (
  input  \вкл_случ_числа ,
  input  \такт ,
  input  \очистка 
);

  wire [7:0] random_1_out, register_1_q, register_2_q, register_3_q, register_4_q, register_5_q,
       register_6_q, register_7_q, register_8_q;

  Random random_1 (.clk(\такт ), .next(\вкл_случ_числа ), .out(random_1_out));  // open: clr
  DotMatrix #(.matrixcols(8), .matrixrows(8)) dotmatrix_1 (
    .col0(register_2_q), .col1(register_1_q), .col2(register_3_q), .col3(register_4_q), .col4(register_5_q),
    .col5(register_6_q), .col6(register_7_q), .col7(register_8_q));
  Register register_1 (.D(register_2_q), .Q(register_1_q), .clk(\такт ), .clr(\очистка ));  // open: en
  Register register_2 (.D(random_1_out), .Q(register_2_q), .clk(\такт ), .clr(\очистка ));  // open: en
  Register register_3 (.D(register_1_q), .Q(register_3_q), .clk(\такт ), .clr(\очистка ));  // open: en
  Register register_4 (.D(register_3_q), .Q(register_4_q), .clk(\такт ), .clr(\очистка ));  // open: en
  Register register_5 (.D(register_4_q), .Q(register_5_q), .clk(\такт ), .clr(\очистка ));  // open: en
  Register register_6 (.D(register_5_q), .Q(register_6_q), .clk(\такт ), .clr(\очистка ));  // open: en
  Register register_7 (.D(register_6_q), .Q(register_7_q), .clk(\такт ), .clr(\очистка ));  // open: en
  Register register_8 (.D(register_7_q), .Q(register_8_q), .clk(\такт ), .clr(\очистка ));  // open: en
  Register register_9 (.D(register_8_q), .clk(\такт ), .clr(\очистка ));  // open: en, Q
endmodule
