// Logisim project alovt2laba.circ as structural Verilog
module \Задание_1  (
  input  [7:0] \набор_данных_1 ,
  input  [7:0] \набор_данных_2 ,
  input  [7:0] \набор_данных_3 ,
  input  [7:0] \набор_данных_4 ,
  input  [1:0] \адрес ,
  input  \вкл_выкл 
);

  wire [7:0] multiplexer_1_out;

  LED led_1 (.in(multiplexer_1_out[5]));
  LED led_2 (.in(multiplexer_1_out[7]));
  LED led_3 (.in(multiplexer_1_out[6]));
  Multiplexer #(.select(2), .width(8)) multiplexer_1 (
    .in0(\набор_данных_1 ), .in1(\набор_данных_2 ), .in2(\набор_данных_3 ), .in3(\набор_данных_4 ),
    .out(multiplexer_1_out), .sel(\адрес ), .en(\вкл_выкл ));
  LED led_4 (.in(multiplexer_1_out[1]));
  LED led_5 (.in(multiplexer_1_out[3]));
  LED led_6 (.in(multiplexer_1_out[4]));
  LED led_7 (.in(multiplexer_1_out[2]));
  LED led_8 (.in(multiplexer_1_out[0]));
endmodule

module \Задание_2  (
  input  [3:0] \набор_данных ,
  input  \вкл_выкл ,
  input  [1:0] \адрес 
);

  wire [3:0] demultiplexer_1_out0, demultiplexer_1_out1, demultiplexer_1_out2, demultiplexer_1_out3;

  Demultiplexer #(.select(2), .width(4)) demultiplexer_1 (
    .out0(demultiplexer_1_out0), .out1(demultiplexer_1_out1), .out2(demultiplexer_1_out2),
    .out3(demultiplexer_1_out3), .in(\набор_данных ), .sel(\адрес ), .en(\вкл_выкл ));
  DotMatrix #(.matrixcols(4), .matrixrows(4)) dotmatrix_1 (
    .col0(demultiplexer_1_out0), .col1(demultiplexer_1_out1), .col2(demultiplexer_1_out2),
    .col3(demultiplexer_1_out3));
endmodule

module \Задание_3  (
  input  in_1,
  input  in_2,
  input  in_3,
  input  in_4,
  input  in_5,
  input  in_6,
  input  in_7,
  input  in_8,
  input  [2:0] \адрес ,
  output out_10
);

  Multiplexer #(.select(3), .enable("false")) multiplexer_1 (
    .in0(in_1), .in1(in_2), .in2(in_3), .in3(in_4), .in4(in_5), .in5(in_6), .in6(in_7), .in7(in_8),
    .out(out_10), .sel(\адрес ));
endmodule

module \Задание_4  (
  input  \вход_0 ,
  input  \вход_1 ,
  input  \вход_2 ,
  input  \вход_3 ,
  input  \адрес_0 ,
  input  \адрес_1 ,
  output out_7
);

  wire not_1_out, not_2_out, not_3_out, not_4_out, not_5_out, not_6_out, \И_2_out , \И_3_out , \И_4_out ,
       \И_out ;

  not not_1 (not_1_out, not_4_out);
  and \u_И  (\И_out , \вход_0 , not_3_out, not_4_out);
  not not_2 (not_2_out, not_3_out);
  and \u_И_2  (\И_2_out , \вход_2 , not_1_out, not_3_out);
  not not_3 (not_3_out, \адрес_0 );
  not not_4 (not_4_out, \адрес_1 );
  not not_5 (not_5_out, not_3_out);
  and \u_И_3  (\И_3_out , \вход_1 , not_4_out, not_2_out);
  not not_6 (not_6_out, not_4_out);
  and \u_И_4  (\И_4_out , \вход_3 , not_6_out, not_5_out);
  or \u_ИЛИ  (out_7, \И_out , \И_3_out , \И_2_out , \И_4_out );
endmodule

module \Задание_6  (
  input  [7:0] \набор_данных_1 ,
  input  [7:0] \набор_данных_2 ,
  input  [7:0] \набор_данных_3 ,
  input  [7:0] \набор_данных_4 ,
  input  [1:0] \адрес ,
  input  \вкл_выкл ,
  output out_7,
  output out_8,
  output out_9,
  output out_10,
  output out_11,
  output out_12,
  output out_13,
  output out_14
);

  Multiplexer #(.select(2), .width(8)) multiplexer_1 (
    .in0(\набор_данных_1 ), .in1(\набор_данных_2 ), .in2(\набор_данных_3 ), .in3(\набор_данных_4 ),
    .out({out_7, out_8, out_9, out_10, out_11, out_12, out_13, out_14}), .sel(\адрес ), .en(\вкл_выкл ));
endmodule
