// Logisim project laba 4.circ as structural Verilog
module \тригер  (
  input  S,
  input  in_2,
  input  in_3,
  input  R
);

  nand nand_1 (in_2, S, in_3);
  nand nand_2 (in_3, in_2, R);
endmodule

module \задание_4  (
  input  J,
  input  K,
  input  C,
  input  Q,
  output S_in,
  output R_in
);

  wire and_1_out, and_2_out, not_1_out;

  and and_1 (and_1_out, J, C);
  not not_1 (not_1_out, Q);
  and and_2 (and_2_out, K, C);
  and and_3 (S_in, and_1_out, not_1_out);
  and and_4 (R_in, and_2_out, Q);
endmodule

module \задание_1  (
  input  in_1,
  input  in_2,
  input  in_3,
  input  in_4,
  input  in_5,
  input  in_6,
  output out_7,
  output out_8
);

  S_R_Flip_Flop s_r_ff_1 (
    .S(in_1), .clk(in_2), .R(in_3), .Q(out_7), .Qn(out_8), .preset(in_4), .reset(in_6), .en(in_5));
endmodule

module \задание_5  (
);

  wire button_1_out, t_ff_1_q, t_ff_1_qn;

  Button button_1 (.out(button_1_out));
  T_Flip_Flop t_ff_1 (.clk(button_1_out), .T(1'b1), .Q(t_ff_1_q), .Qn(t_ff_1_qn));  // open: preset, reset, en
  LED led_1 (.in(t_ff_1_q));
  LED led_2 (.in(t_ff_1_qn));
endmodule
