// Logisim project labaALOVT.circ as structural Verilog: 4 circuits, main circuit main
module main (
  input  v,
  input  x1,
  input  x2,
  output q0,
  output q1,
  output q2,
  output q3
);

  wire not_1_out, not_2_out;

  not not_1 (not_1_out, x1);
  not not_2 (not_2_out, x2);
  and and_1 (q0, v, not_1_out, not_2_out);
  and and_2 (q1, v, x2, not_1_out);
  and and_3 (q2, v, x1, not_2_out);
  and and_4 (q3, v, x1, x2);
endmodule

module \Задание_1  (
  input  v,
  input  x0,
  input  x1,
  input  [2:0] in_4,
  input  x3,
  output q0,
  output q1,
  output q2,
  output q3,
  output q4,
  output q5,
  output q6,
  output q7
);

  Demultiplexer #(.select(3)) demultiplexer_1 (
    .out0(q0), .out1(q1), .out2(q2), .out3(q3), .out4(q4), .out5(q5), .out6(q6), .out7(q7), .in(v), .sel(in_4));  // open: en

  assign x0 = in_4[0];
  assign x1 = in_4[1];
  assign x3 = in_4[2];
endmodule

module \Задание_3  (
  input  x1,
  input  x2,
  input  x3,
  output y1,
  output y2,
  output y3
);

  wire and_1_out, and_2_out, and_3_out, and_4_out, not_1_out, not_2_out, not_3_out, not_4_out, not_5_out,
       not_6_out;

  not not_1 (not_1_out, x1);
  not not_2 (not_2_out, x2);
  not not_3 (not_3_out, x1);
  not not_4 (not_4_out, x2);
  not not_5 (not_5_out, x3);
  not not_6 (not_6_out, x3);
  and and_1 (and_1_out, not_1_out, x2);
  and and_2 (and_2_out, not_2_out, x1);
  and and_3 (and_3_out, x1, x2);
  and and_4 (and_4_out, not_3_out, not_4_out, not_5_out);
  or or_1 (y2, x1, x2, not_6_out);
  or or_2 (y3, and_1_out, and_2_out);
  or or_3 (y1, and_3_out, and_4_out);
endmodule

module \Задание_2  (
  input  v,
  input  x0,
  input  x1,
  output q0,
  output q1,
  output q2,
  output q3
);

  wire not_1_out, not_2_out, not_3_out, not_4_out;

  not not_1 (not_1_out, x0);
  and and_1 (q0, v, not_1_out, not_2_out);
  not not_2 (not_2_out, x1);
  and and_2 (q1, v, x0, not_3_out);
  not not_3 (not_3_out, x1);
  not not_4 (not_4_out, x0);
  and and_3 (q2, not_4_out, x1, v);
  and and_4 (q3, x0, x1, v);
endmodule
