// Logisim project лаба3.circ as structural Verilog
module \задание_1  (
  input  in_1,
  input  [7:0] in_2,
  input  [7:0] in_3,
  output [7:0] out_4,
  output out_5
);

  Adder adder_1 (.a(in_2), .b(in_3), .out(out_4), .cin(in_1), .cout(out_5));
endmodule

module \задание_2  (
  input  A,
  input  B,
  output S,
  output C
);

  wire and_2_out, and_3_out, not_1_out, not_2_out;

  not not_1 (not_1_out, A);
  not not_2 (not_2_out, B);
  and and_1 (C, A, B);
  and and_2 (and_2_out, not_1_out, B);
  and and_3 (and_3_out, A, not_2_out);
  or or_1 (S, and_2_out, and_3_out);
endmodule

module \задание_3  (
  input  A,
  input  B,
  input  Cin,
  output S,
  output C
);

  wire and_1_out, and_2_out, and_3_out, and_4_out, and_5_out, and_6_out, and_7_out, and_8_out, and_9_out,
       and_10_out, and_11_out, not_1_out, not_2_out, not_3_out, not_4_out, not_5_out, not_6_out, or_1_out,
       or_3_out, or_4_out;

  not not_1 (not_1_out, A);
  not not_2 (not_2_out, B);
  not not_3 (not_3_out, A);
  not not_4 (not_4_out, B);
  and and_1 (and_1_out, B, Cin);
  and and_2 (and_2_out, A, Cin);
  and and_3 (and_3_out, not_1_out, not_2_out);
  and and_4 (and_4_out, not_3_out, B);
  not not_5 (not_5_out, Cin);
  and and_5 (and_5_out, A, not_4_out);
  not not_6 (not_6_out, Cin);
  and and_6 (and_6_out, A, B);
  or or_1 (or_1_out, and_1_out, and_2_out);
  and and_7 (and_7_out, A, B);
  and and_8 (and_8_out, and_3_out, Cin);
  and and_9 (and_9_out, and_4_out, not_5_out);
  and and_10 (and_10_out, and_5_out, not_6_out);
  and and_11 (and_11_out, and_6_out, Cin);
  or or_2 (C, or_1_out, and_7_out);
  or or_3 (or_3_out, and_8_out, and_9_out);
  or or_4 (or_4_out, and_10_out, and_11_out);
  or or_5 (S, or_3_out, or_4_out);
endmodule

module \задание_4  (
  input  in_1,
  input  A,
  input  B,
  input  A_2,
  input  B_2,
  input  A_3,
  input  B_3,
  input  A_4,
  input  B_4,
  input  A_5,
  input  B_5,
  input  A_6,
  input  B_6,
  input  A_7,
  input  B_7,
  input  A_8,
  input  B_8,
  output out_18,
  output out_19,
  output out_20,
  output out_21,
  output out_22,
  output out_23,
  output out_24,
  output out_25,
  output \если_сумма_больше_255 
);

  wire \задание_3_1_c , \задание_3_2_c , \задание_3_3_c , \задание_3_4_c , \задание_3_5_c , \задание_3_6_c ,
       \задание_3_7_c ;

  \задание_3  \u_задание_3_1  (.A(A), .B(B), .Cin(in_1), .S(out_18), .C(\задание_3_1_c ));
  \задание_3  \u_задание_3_2  (.A(A_2), .B(B_2), .Cin(\задание_3_1_c ), .S(out_19), .C(\задание_3_2_c ));
  \задание_3  \u_задание_3_3  (.A(A_3), .B(B_3), .Cin(\задание_3_2_c ), .S(out_20), .C(\задание_3_3_c ));
  \задание_3  \u_задание_3_4  (.A(A_4), .B(A_4), .Cin(\задание_3_3_c ), .S(out_21), .C(\задание_3_4_c ));
  \задание_3  \u_задание_3_5  (.A(A_5), .B(B_5), .Cin(\задание_3_4_c ), .S(out_22), .C(\задание_3_5_c ));
  \задание_3  \u_задание_3_6  (.A(A_6), .B(B_6), .Cin(\задание_3_5_c ), .S(out_23), .C(\задание_3_6_c ));
  \задание_3  \u_задание_3_7  (.A(A_7), .B(B_7), .Cin(\задание_3_6_c ), .S(out_24), .C(\задание_3_7_c ));
  \задание_3  \u_задание_3_8  (.A(A_8), .B(B_8), .Cin(\задание_3_7_c ), .S(out_25), .C(\если_сумма_больше_255 ));

  assign B_4 = A_4;
endmodule

module \задание_5  (
  input  [6:0] in_1
);

  wire button_1_out, comparator_1_eq, comparator_1_gt, comparator_1_lt, or_1_out;
  wire [6:0] keyboard_1_data;

  Keyboard keyboard_1 (.clr(button_1_out), .data(keyboard_1_data));  // open: clk, re, avail
  Button button_1 (.out(button_1_out));
  Comparator #(.width(7)) comparator_1 (
    .a(keyboard_1_data), .b(in_1), .gt(comparator_1_gt), .eq(comparator_1_eq), .lt(comparator_1_lt));
  LED led_1 (.in(or_1_out));
  LED led_2 (.in(comparator_1_eq));
  or or_1 (or_1_out, comparator_1_gt, comparator_1_lt);
endmodule

module \задание_6  (
  input  A,
  input  B,
  output More,
  output Less,
  output Equal
);

  wire and_3_out, and_4_out, not_1_out, not_2_out, not_3_out, not_4_out;

  not not_1 (not_1_out, B);
  not not_2 (not_2_out, A);
  not not_3 (not_3_out, A);
  not not_4 (not_4_out, B);
  and and_1 (More, A, not_1_out);
  and and_2 (Less, not_2_out, B);
  and and_3 (and_3_out, not_3_out, not_4_out);
  and and_4 (and_4_out, A, B);
  or or_1 (Equal, and_3_out, and_4_out);
endmodule

module \задание_7  (
  input  A,
  input  B,
  input  A_2,
  input  B_2,
  input  A_3,
  input  B_3,
  input  A_4,
  input  B_4,
  input  A_5,
  input  B_5,
  input  A_6,
  input  B_6,
  input  A_7,
  input  B_7,
  input  A_8,
  input  B_8
);

  \задание_6  \u_задание_6_1  (.A(A), .B(B));  // open: More, Less, Equal
  \задание_6  \u_задание_6_2  (.A(A_2), .B(B_2));  // open: More, Less, Equal
  \задание_6  \u_задание_6_3  (.A(A_3), .B(B_3));  // open: More, Less, Equal
  \задание_6  \u_задание_6_4  (.A(A_4), .B(B_4));  // open: More, Less, Equal
  \задание_6  \u_задание_6_5  (.A(A_5), .B(B_5));  // open: More, Less, Equal
  \задание_6  \u_задание_6_6  (.A(A_6), .B(B_6));  // open: More, Less, Equal
  \задание_6  \u_задание_6_7  (.A(A_7), .B(B_7));  // open: More, Less, Equal
  \задание_6  \u_задание_6_8  (.A(A_8), .B(B_8));  // open: More, Less, Equal
endmodule
